# Fritzing sketch op-amp2 (saved by Fritzing 0.8.5b)
breadboards: 1

parts:
  U1 = LM 358 Dual Op-Amp [package="DIP8 [THT]"]
  TRS1 = Audio Jack (TRS) 3.5mm [package="4Ucon 08780 [THT]"]
  R1 = Resistor [tolerance=±5% resistance=10k package=THT]
  R2 = Resistor [tolerance=±5% resistance=10k package=THT]
  R3 = Resistor [tolerance=±5% resistance=100k package=THT]
  R4 = Resistor [tolerance=±5% resistance=120 package=THT]
  C1 = Electrolytic Capacitor [capacitance=1µF package="100 mil [THT, electrolytic]"]
  R5 = Resistor [tolerance=±5% resistance=10k package=THT]

nets:
  N1: U1.connector0, R3.Pin_0, R4.Pin_1
  N2: U1.connector1, R3.Pin_1, R5.Pin_0
  N3: U1.connector2, R1.Pin_0, R2.Pin_0
  GND: U1.connector3, TRS1.Sleeve, C1.-, R5.Pin_1
  5V: U1.connector7
  N4: TRS1.Ring, R2.Pin_1
  N5: TRS1.Tip, R1.Pin_1
  N6: R4.Pin_0, C1.+
